# Fritzing sketch algenlogger_hauptsteckbrett (saved by Fritzing 0.9.3b)
breadboards: 3

parts:
  U1 = ESP32S-HiLetgo [part_number=ESP32S-HiLetgo]
  Grove1 = Grove Light Sensor
  DS1 = DS18B20 1-Wire Temperature Sensor [part_number=DS18B20]
  M1 = DC Motor
  Reg1 = DC-DC CONVERTER [part_number=80633 package=dc-dc_converter]
  Reg2 = DC-DC CONVERTER [part_number=80633 package=dc-dc_converter]
  JP1 = USB_MICROB_PLUG [package=micro-b-th]
  Q7 = MOSFET-NCHANNEL [package=to-92]
  LED1 = LED - 3mm [color="Red (633nm)" package="3 mm [THT]"]
  U2 = WS2812 RGB LED strip
  Q8 = Basic FET P-Channel [package="D2Pak [SMD]"]
  Q9 = Basic FET P-Channel [package="D2Pak [SMD]"]
  Q10 = Basic FET P-Channel [package="D2Pak [SMD]"]
  R3 = Resistor [tolerance=±1% resistance=4.7k package="1206 [SMD]"]

nets:
  VCC: U1.3.3, Grove1.VCC, DS1.VDD, Reg1.OUT+, Reg2.OUT-, R3.Pin_0
  GND: U1.GND, Grove1.GND, DS1.GND, Q8.Gate, Q9.Gate, Q10.Gate
  N1: U1.GPIO15, Q9.source
  N2: U1.GPIO4, DS1.DQ, R3.Pin_1
  N3: U1.GPIO18, Q8.source
  N4: U1.GPIO23, Q10.source
  N5: M1.pin_1, Q9.drain
  N6: M1.pin_2, Reg1.OUT-, LED1.anode
  N7: Reg1.IN-, Reg2.IN-, JP1.GND
  N8: Reg1.IN+, JP1.D+
  N9: Reg2.OUT+, U2.VCC, U2.DOUT
  N10: Q7.D, Q10.drain
  N11: Q7.G, LED1.cathode
  N12: U2.GND, Q8.drain

custom parts:
  ESP32S-HiLetgo: HiLetgo ESP-WROOM-32 ESP32 ESP-32S Development Board 2.4GHz Dual-Mode WiFi + Bluetooth Dual Cores Microcontroller The ESP32 integrated with Antenna switches, RF Balun, power amplifiers, low-noise amplifiers, filters, and management modules, and the entire solution occupies the least area of PCB. 2.4 GHz Wi-Fi plus Bluetooth dual-mode chip, with TSMC Ultra-low power consumption 40nm technology,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
  DC-DC CONVERTER: WYHP 5A constant current/voltage manufactured by Shenzhen Weiyapuhua Technology Co., Ltd
  WS2812 RGB LED strip: WS2812 strip
