# Fritzing sketch led-phot-arduino (saved by Fritzing 0.9.3b)
breadboards: 1

parts:
  Bauteil1 = Arduino Uno (Rev3) - ICSP
  R2 = Resistor [tolerance=±5% resistance=1k package=THT]
  LED1 = LED - 5mm [color="Red (633nm)" package="5 mm [THT]"]
  R3 = Photocell (LDR) [package=THT]
  R1 = Resistor [tolerance=±5% resistance=220 package=THT]

nets:
  N1: Bauteil1.A0, R3.pin_0
  N2: Bauteil1.5V, LED1.anode, R3.pin_1
  N3: Bauteil1.GND, R2.Pin_0, R1.Pin_0
  N4: LED1.cathode, R1.Pin_1
