# Fritzing sketch led-phot-simple (saved by Fritzing 0.9.3b)
breadboards: 1

parts:
  R1 = Resistor [tolerance=±5% resistance=220 package=THT]
  R2 = Resistor [tolerance=±5% resistance=1k package=THT]
  LED1 = LED - 5mm [color="Red (633nm)" package="5 mm [THT]"]
  R3 = Photocell (LDR) [package=THT]

nets:
  N1: R1.Pin_0, R2.Pin_0
  N2: R1.Pin_1, LED1.cathode
  N3: LED1.anode, R3.pin_1

notes:
  zum Voltmeter
