# Fritzing sketch led-phot_digital+analog-arduino (saved by Fritzing 0.9.3b)
breadboards: 1

parts:
  Bauteil1 = Arduino Uno (Rev3) - ICSP
  R2 = Resistor [tolerance=±5% resistance=1k package=THT]
  LED1 = LED - 5mm [color="Red (633nm)" package="5 mm [THT]"]
  R3 = Photocell (LDR) [package=THT]
  R1 = Resistor [tolerance=±5% resistance=220 package=THT]
  o1 = Module display OLED I2C 128x64 SSD1306 [package=THT]
  Часть2 = BH1750

nets:
  N1: Bauteil1.A0, R3.pin_0
  N2: Bauteil1.A4/SDA, o1.SDA, Часть2.SDA
  N3: Bauteil1.A5/SCL, o1.SCL, Часть2.SCL
  VCC: Bauteil1.5V, LED1.anode, R3.pin_1, o1.VCC, Часть2.VCC
  GND: Bauteil1.GND, R2.Pin_0, R1.Pin_0, o1.GND, Часть2.GND
  N4: LED1.cathode, R1.Pin_1

custom parts:
  Module display OLED I2C 128x64 SSD1306: Ecran OLED I2C SSD163 de 128x64 avec connexion I2C
  BH1750: Light Sensor
