# Fritzing sketch led-blink (saved by Fritzing 0.9.3b)
breadboards: 1

parts:
  Bauteil1 = Arduino Uno (Rev3) - ICSP
  LED1 = LED - 5mm [color="Green (570nm)" package="5 mm [THT]"]
  R1 = Resistor [tolerance=±5% resistance=330 package=THT]

nets:
  N1: Bauteil1.D13/SCK, R1.Pin_1
  N2: Bauteil1.GND, LED1.cathode
  N3: LED1.anode, R1.Pin_0
